# Fritzing sketch led (saved by Fritzing 0.9.2b)
breadboards: 1

parts:
  Raspberry_Pi_1 = Raspberry Pi 3 [part_number=RPI-3-V1.2]
  LED1 = smd LED [color="Red (633nm)" package="0805 [SMD]"]
  LED2 = smd LED [color="Green (555nm)" package="0805 [SMD]"]
  LED3 = smd LED [color="Blue (430nm)" package="0805 [SMD]"]

nets:
  N1: Raspberry_Pi_1.GND, LED1.cathode, LED2.cathode, LED3.cathode
  N2: Raspberry_Pi_1.GIPO18, LED3.anode
  N3: Raspberry_Pi_1.GIPO15, LED2.anode
  N4: Raspberry_Pi_1.GIPO14, LED1.anode
