# Fritzing sketch push (saved by Fritzing 0.9.2b)
breadboards: 1

parts:
  Raspberry_Pi_1 = Raspberry Pi 3 [part_number=RPI-3-V1.2]
  LED1 = smd LED [color="Red (633nm)" package="0805 [SMD]"]
  S1 = Pushbutton [package="[SMD]"]

nets:
  N1: Raspberry_Pi_1.GIPO23, S1.Pin_1, S1.Pin_2
  N2: Raspberry_Pi_1.GIPO14, LED1.anode
  N3: Raspberry_Pi_1.GND, LED1.cathode, S1.Pin_3, S1.Pin_4
